# Fritzing sketch energy-node (saved by Fritzing 1.0.3b)
breadboards: 1

parts:
  M1 = DOIT Esp32 DevKit v1 (30 pins long, 11 pins width) [part_number=ESP32S-PIN30]
  SCT-013_2 = Microphone
  SCT-013_1 = Microphone
  R1 = Resistor [tolerance=±5% resistance=33 package="2512 [SMD]"]
  R2 = Resistor [tolerance=±5% resistance=33 package="2512 [SMD]"]
  R3 = Resistor [tolerance=±5% resistance=33 package="2512 [SMD]"]
  R4 = Resistor [tolerance=±5% resistance=33 package="2512 [SMD]"]
  R5 = Resistor [tolerance=±5% resistance=470k package="2512 [SMD]"]
  R6 = Resistor [tolerance=±5% resistance=470k package="2512 [SMD]"]
  R7 = Resistor [tolerance=±5% resistance=470k package="2512 [SMD]"]
  R8 = Resistor [tolerance=±5% resistance=470k package="2512 [SMD]"]
  C2 = Electrolytic Capacitor [capacitance=10µF voltage=35V package="100 mil [THT, electrolytic]"]
  C3 = Electrolytic Capacitor [capacitance=10µF voltage=35V package="100 mil [THT, electrolytic]"]

nets:
  N1: M1.3V3, R5.Pin_1, R6.Pin_1
  N2: M1.GND, R7.Pin_0, R8.Pin_0, C2.-, C3.-
  N3: M1.D34, SCT-013_1.pin2, R3.Pin_0, R4.Pin_0
  N4: M1.D33, SCT-013_2.pin2, R1.Pin_0, R2.Pin_0
  N5: SCT-013_2.pin1, R1.Pin_1, R2.Pin_1, R5.Pin_0, R7.Pin_1, C2.+
  N6: SCT-013_1.pin1, R3.Pin_1, R4.Pin_1, R6.Pin_0, R8.Pin_1, C3.+

custom parts:
  DOIT Esp32 DevKit v1 (30 pins long, 11 pins width): The DOIT Esp32 DevKit v1 is one of the development board created by DOIT to evaluate the ESP-WROOM-32 module. It is based on the ESP32 microcontroller that boasts Wifi, Bluetooth, Ethernet and Low Power support all in a single chip. (vanepp) made breadboard work, adjusted pin numbering and labels and reduced size of schematic and cleaned up pcb. This chip is 30pins long (2 x15) and 11 pins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
