# Fritzing sketch temp-node (saved by Fritzing 1.0.3b)
breadboards: 1

parts:
  DS1 = DS18B20 1-Wire Temperature Sensor Probe
  DS2 = DS18B20 1-Wire Temperature Sensor Probe
  M1 = DOIT Esp32 DevKit v1 (30 pins long, 11 pins width) [part_number=ESP32S-PIN30]

nets:
  GND: DS1.GND, DS2.GND, M1.GND
  N1: DS1.DQ, DS2.DQ, M1.D4
  VDD: DS1.VDD, DS2.VDD, M1.VIN

custom parts:
  DOIT Esp32 DevKit v1 (30 pins long, 11 pins width): The DOIT Esp32 DevKit v1 is one of the development board created by DOIT to evaluate the ESP-WROOM-32 module. It is based on the ESP32 microcontroller that boasts Wifi, Bluetooth, Ethernet and Low Power support all in a single chip. (vanepp) made breadboard work, adjusted pin numbering and labels and reduced size of schematic and cleaned up pcb. This chip is 30pins long (2 x15) and 11 pins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
