# Fritzing sketch water-flow-node (saved by Fritzing 1.0.3b)
breadboards: 1

parts:
  YF-S201_Flow_Meter2 = YF-S201 Water Flow Meter
  M1 = DOIT Esp32 DevKit v1 (30 pins long, 11 pins width) [part_number=ESP32S-PIN30]

nets:
  N1: YF-S201_Flow_Meter2.SIG, M1.D12
  GND: YF-S201_Flow_Meter2.GND, M1.GND
  VCC: YF-S201_Flow_Meter2.VCC, M1.VIN

custom parts:
  YF-S201 Water Flow Meter: The YF-S201 Flow Meter. The input voltage is 5V to 24V (DC).
  DOIT Esp32 DevKit v1 (30 pins long, 11 pins width): The DOIT Esp32 DevKit v1 is one of the development board created by DOIT to evaluate the ESP-WROOM-32 module. It is based on the ESP32 microcontroller that boasts Wifi, Bluetooth, Ethernet and Low Power support all in a single chip. (vanepp) made breadboard work, adjusted pin numbering and labels and reduced size of schematic and cleaned up pcb. This chip is 30pins long (2 x15) and 11 pins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
